// Logisim project Processeur Kathleen 16.circ as structural Verilog: 5 circuits, main circuit UAL
module UAL (
  input  [15:0] V1,
  input  [15:0] V2,
  input  [1:0] ctrAlu,
  output [1:0] ZF_CF,
  output [15:0] Sortie
);

  wire adder_1_cout, subtractor_1_bout;
  wire [15:0] adder_1_out, nand_1_out, subtractor_1_out;

  Adder #(.width(16)) adder_1 (.a(V1), .b(V2), .out(adder_1_out), .cout(adder_1_cout));  // open: cin
  Subtractor #(.width(16)) subtractor_1 (
    .a(V1), .b(V2), .out(subtractor_1_out), .bout(subtractor_1_bout));  // open: bin
  assign nand_1_out = ~(V1 & V2);  // NAND_Gate nand_1, 16 bits wide
  Comparator #(.width(16)) comparator_1 (.a({16{1'b0}}), .b(Sortie), .eq(ZF_CF[0]));  // open: gt, lt
  Multiplexer #(.select(2), .width(16)) multiplexer_1 (
    .in0(adder_1_out), .in1(subtractor_1_out), .in2(nand_1_out), .out(Sortie), .sel(ctrAlu));  // open: in3, en
  or or_1 (ZF_CF[1], adder_1_cout, subtractor_1_bout);
endmodule

// 10|16
module Extenseur (
  input  [9:0] in_1,
  output [15:0] out_2
);

  wire [15:0] bit_extender_1_out;

  assign bit_extender_1_out = {{6{1'b0}}, in_1};  // Bit_Extender bit_extender_1
  Shifter #(.width(16)) shifter_1 (.in(bit_extender_1_out), .\dist (4'b0110), .out(out_2));
endmodule

module Banc_de_registre (
  input  [2:0] rc_ra,
  input  [2:0] ra,
  input  EnableWrite,
  input  Clock,
  input  [2:0] rb,
  input  Reset,
  input  [15:0] \Entrée ,
  output [15:0] S1,
  output [15:0] S2
);

  wire and_1_out, and_2_out, and_3_out, and_4_out, and_5_out, and_6_out, and_7_out, and_8_out, R0, R1, R2,
       R3, R4, R5, R6, R7;
  wire [15:0] k1, k2, k3, k4, k5, k6, k7, k8;

  Decoder #(.select(3)) decoder_1 (
    .out0(R0), .out1(R1), .out2(R2), .out3(R3), .out4(R4), .out5(R5), .out6(R6), .out7(R7), .sel(ra));  // open: en
  and and_1 (and_1_out, R0, EnableWrite);
  and and_2 (and_2_out, R1, EnableWrite);
  and and_3 (and_3_out, R2, EnableWrite);
  and and_4 (and_4_out, R3, EnableWrite);
  and and_5 (and_5_out, R4, EnableWrite);
  and and_6 (and_6_out, R5, EnableWrite);
  and and_7 (and_7_out, R6, EnableWrite);
  and and_8 (and_8_out, R7, EnableWrite);
  Register #(.width(16)) u_R0 (.D(\Entrée ), .en(and_1_out), .Q(k1), .clk(Clock), .clr(Reset));
  Register #(.width(16)) u_R1 (.D(\Entrée ), .en(and_2_out), .Q(k2), .clk(Clock), .clr(Reset));
  Register #(.width(16)) u_R2 (.D(\Entrée ), .en(and_3_out), .Q(k3), .clk(Clock), .clr(Reset));
  Register #(.width(16)) u_R3 (.D(\Entrée ), .en(and_4_out), .Q(k4), .clk(Clock), .clr(Reset));
  Register #(.width(16)) u_R4 (.D(\Entrée ), .en(and_5_out), .Q(k5), .clk(Clock), .clr(Reset));
  Register #(.width(16)) u_R5 (.D(\Entrée ), .en(and_6_out), .Q(k6), .clk(Clock), .clr(Reset));
  Register #(.width(16)) u_R6 (.D(\Entrée ), .en(and_7_out), .Q(k7), .clk(Clock), .clr(Reset));
  Register #(.width(16)) u_R7 (.D(\Entrée ), .en(and_8_out), .Q(k8), .clk(Clock), .clr(Reset));
  Multiplexer #(.select(3), .width(16)) multiplexer_1 (
    .in0(k1), .in1(k2), .in2(k3), .in3(k4), .in4(k5), .in5(k6), .in6(k7), .in7(k8), .out(S1), .sel(rc_ra));  // open: en
  Multiplexer #(.select(3), .width(16)) multiplexer_2 (
    .in0(k1), .in1(k2), .in2(k3), .in3(k4), .in4(k5), .in5(k6), .in6(k7), .in7(k8), .out(S2), .sel(rb));  // open: en

  // Other names for the same wires on the sheet: C = Clock; E = EnableWrite; R = Reset
endmodule

module IFU (
  input  [15:0] in_1,
  input  CLOCK,
  input  RESET,
  input  [15:0] DestjALR,
  input  ZF,
  output [2:0] rc,
  output [2:0] rb,
  output EnableWrite,
  output [2:0] ra,
  output [6:0] imm_7,
  output [9:0] imm_10,
  output MemWrite,
  output isSWorBEQ,
  output [1:0] InSrc,
  output isADDIorLWorSW,
  output [1:0] ctrALU,
  output [15:0] PC_1,
  output [15:0] PC
);

  wire add, addi, and_1_out, beq, jalr, lui, lw, \nand , priority_encoder_1_p5, priority_encoder_2_p2, RRi,
       RRR;
  wire [2:0] padding;
  wire [6:0] multiplexer_2_out;
  wire [6:3] controlled_buffer_2_out;
  wire [15:0] adder_2_out, bit_extender_1_out, multiplexer_1_out;

  Decoder #(.select(3)) decoder_1 (
    .out0(add), .out1(addi), .out2(\nand ), .out3(lui), .out4(MemWrite), .out5(lw), .out6(beq), .out7(jalr),
    .sel(in_1[15:13]));  // open: en
  assign {ra, imm_10} = lui ? in_1[12:0] : 13'bz;  // Controlled_Buffer controlled_buffer_1
  Multiplexer #(.width(16)) multiplexer_1 (
    .in0(PC_1), .in1(DestjALR), .out(multiplexer_1_out), .sel(jalr));  // open: en
  assign {rb, padding, controlled_buffer_2_out, rc} = RRR ? in_1[12:0] : 13'bz;  // Controlled_Buffer controlled_buffer_2
  assign {ra, rb, imm_7} = RRi ? in_1[12:0] : 13'bz;  // Controlled_Buffer controlled_buffer_3
  Register #(.width(16)) register_1 (.D(adder_2_out), .Q(PC), .clk(CLOCK), .clr(RESET));  // open: en
  // Priority_Encoder #(.select(2)) priority_encoder_1: pin names not known; wires that end beside it: InSrc, lui, jalr, lw, priority_encoder_1_p5
  or or_1 (priority_encoder_1_p5, add, addi, \nand );
  Adder #(.width(16)) adder_1 (.a(PC), .b(16'h1), .out(PC_1));  // open: cin, cout
  or or_2 (EnableWrite, add, addi, \nand , lui, lw, jalr);
  Multiplexer #(.width(7)) multiplexer_2 (
    .in0({7{1'b0}}), .in1(imm_7), .out(multiplexer_2_out), .sel(and_1_out));  // open: en
  and and_1 (and_1_out, ZF, beq);
  assign bit_extender_1_out = {{9{multiplexer_2_out[6]}}, multiplexer_2_out};  // Bit_Extender bit_extender_1
  // Priority_Encoder #(.select(2)) priority_encoder_2: pin names not known; wires that end beside it: ctrALU, priority_encoder_2_p2, beq, \nand 
  or or_3 (isSWorBEQ, MemWrite, beq);
  or or_4 (isADDIorLWorSW, MemWrite, lw);
  or or_5 (priority_encoder_2_p2, add, addi);
  Adder #(.width(16)) adder_2 (.a(multiplexer_1_out), .b(bit_extender_1_out), .out(adder_2_out));  // open: cin, cout
  or or_6 (RRR, add, \nand );
  or or_7 (RRi, addi, MemWrite, lw, beq, jalr);

  // Other names for the same wires on the sheet: opcode[2:0] = in_1[15:13]; RI = lui; sw = MemWrite
endmodule

module processeur_Kathleen (
);

  wire Clock, EnableWrite, isADDIorLWorSW, isSworBeQ, Memwrite, Reset, ZF;
  wire [0:0] ual_1_zf_cf;
  wire [1:0] ctrALU, inSrc;
  wire [2:0] multiplexer_2_out, ra, rb, rc;
  wire [6:0] imm_7;
  wire [9:0] imm_10;
  wire [15:0] banc_de_registre_1_s1, bit_extender_1_out, datain, dataout, destjalr, extenseur_1_out_2,
       ifu_1_pc, multiplexer_1_out, multiplexer_3_out, PC_1, rom_1_data, ual_1_sortie;

  RAM #(.addrWidth(16), .dataWidth(16), .bus("separate")) ram_1 (
    .addr(ual_1_sortie), .din(datain), .data(dataout), .str(Memwrite), .clk(Clock));  // open: sel, ld, clr
  Extenseur extenseur_1 (.in_1(imm_10), .out_2(extenseur_1_out_2));
  Multiplexer #(.select(2), .width(16)) multiplexer_1 (
    .in0(extenseur_1_out_2), .in1(PC_1), .in2(dataout), .in3(ual_1_sortie), .out(multiplexer_1_out),
    .sel(inSrc));  // open: en
  IFU ifu_1 (
    .in_1(rom_1_data), .rc(rc), .rb(rb), .EnableWrite(EnableWrite), .ra(ra), .imm_7(imm_7), .imm_10(imm_10),
    .MemWrite(Memwrite), .isSWorBEQ(isSworBeQ), .InSrc(inSrc), .isADDIorLWorSW(isADDIorLWorSW),
    .ctrALU(ctrALU), .CLOCK(Clock), .RESET(Reset), .DestjALR(destjalr), .PC_1(PC_1), .PC(ifu_1_pc), .ZF(ZF));
  Multiplexer #(.width(3)) multiplexer_2 (.in0(rc), .in1(ra), .out(multiplexer_2_out), .sel(isSworBeQ));  // open: en
  Banc_de_registre banc_de_registre_1 (
    .rc_ra(multiplexer_2_out), .EnableWrite(EnableWrite), .rb(rb), .Clock(Clock), .Reset(Reset),
    .\Entrée (multiplexer_1_out), .S2(datain), .ra(ra), .S1(banc_de_registre_1_s1));
  assign bit_extender_1_out = {{9{imm_7[6]}}, imm_7};  // Bit_Extender bit_extender_1
  Multiplexer #(.width(16)) multiplexer_3 (
    .in0(datain), .in1(bit_extender_1_out), .out(multiplexer_3_out), .sel(isADDIorLWorSW));  // open: en
  ROM #(.addrWidth(16), .dataWidth(16)) rom_1 (.addr(ifu_1_pc), .data(rom_1_data));  // open: sel
  UAL ual_1 (
    .V1(banc_de_registre_1_s1), .V2(multiplexer_3_out), .Sortie(ual_1_sortie), .ctrAlu(ctrALU),
    .ZF_CF({ZF, ual_1_zf_cf[0]}));

  // Notes on the sheet:
  //   Données
  //   contents of rom_1 (hex, n*v repeats v):
  //   1111 2222 3333 4444 5555 6666 7777 1111 2222 3333 4444 5555 6666 7777 8888 8888
endmodule
